# Fritzing sketch hardware_schematic (saved by Fritzing 1.0.3b)

parts:
  S1 = Round Pushbutton
  S2 = Round Pushbutton
  S3 = Round Pushbutton
  S4 = Round Pushbutton
  A2 = lilygo internet poe

nets:
  N1: S1.leg0, A2.Pin_6
  N2: S1.leg1, S2.leg1, S3.leg1, S4.leg1, A2.Pin_9, A2.Pin_10
  N3: S2.leg0, A2.Pin_13
  N4: S3.leg0, A2.Pin_14
  N5: S4.leg0, A2.Pin_5

custom parts:
  lilygo internet poe: LILYGO® TTGO T-Internet-POE ESP32-WROOM LAN8720A Chip Ethernet Adapter And Downloader Expansion Board Programmable Hardware.
